// Logisim project P3_L0.circ as structural Verilog: 9 circuits, main circuit main
module main (
  input  reset,
  output [31:0] out_2,
  output [31:0] out_3,
  output out_4,
  output [4:0] out_5,
  output [31:0] out_6,
  output out_7,
  output [31:0] out_8,
  output [31:0] out_9
);

  wire alu_1_zero, and_1_out, clk, controlunit_1_alusrc, controlunit_1_memread, controlunit_1_memtoreg,
       controlunit_1_pcsrc, controlunit_1_regdst, ExtOp, SignOp;
  wire [1:0] alucontrol_1_aluop_2;
  wire [2:0] controlunit_1_aluop_2_0;
  wire [31:0] adder_2_out, adder_3_out, ext_1_result, grf_1_rd1, multiplexer_3_out, multiplexer_4_out,
       multiplexer_5_out, pc, ram_1_data, shifter_1_out, signext_1_result;

  Clock u_clk (.out(clk));
  Register #(.width(32)) u_PC (.D(multiplexer_4_out), .Q(pc), .clk(clk), .clr(reset));  // open: en
  Adder #(.width(32)) adder_1 (.a(pc), .b(32'h3000), .out(out_3));  // open: cin, cout
  ROM #(.addrWidth(12), .dataWidth(32)) rom_1 (.addr(pc[13:2]), .data(out_2));  // open: sel
  Adder #(.width(32)) adder_2 (.a(pc), .b(32'h4), .out(adder_2_out));  // open: cin, cout
  ControlUnit controlunit_1 (
    .Op(out_2[31:26]), .RegDst(controlunit_1_regdst), .PCSrc(controlunit_1_pcsrc),
    .MemtoReg(controlunit_1_memtoreg), .MemWrite(out_7), .MemRead(controlunit_1_memread),
    .ALUOp_2_0(controlunit_1_aluop_2_0), .SignOp(SignOp), .ExtOp(ExtOp), .ALUSrc(controlunit_1_alusrc),
    .RegWrite(out_4));
  Multiplexer #(.width(5)) multiplexer_1 (
    .in0(out_2[20:16]), .in1(out_2[15:11]), .out(out_5), .sel(controlunit_1_regdst));  // open: en
  SIGNext signext_1 (.Input(out_2[15:0]), .Result(signext_1_result), .SignOp(SignOp));
  EXT ext_1 (.Input(out_2[15:0]), .Result(ext_1_result));
  Multiplexer #(.width(32)) multiplexer_2 (
    .in0(multiplexer_5_out), .in1(ext_1_result), .out(out_6), .sel(ExtOp));  // open: en
  GRF grf_1 (
    .Rr1(out_2[25:21]), .Rr2(out_2[20:16]), .Wr(out_5), .WD(out_6), .RD1(grf_1_rd1), .RD2(out_9), .clk(clk),
    .reset(reset), .we(out_4));
  Shifter #(.width(32)) shifter_1 (.in(signext_1_result), .\dist (5'b00010), .out(shifter_1_out));
  Multiplexer #(.width(32)) multiplexer_3 (
    .in0(out_9), .in1(signext_1_result), .out(multiplexer_3_out), .sel(controlunit_1_alusrc));  // open: en
  Adder #(.width(32)) adder_3 (.a(adder_2_out), .b(shifter_1_out), .out(adder_3_out));  // open: cin, cout
  ALU alu_1 (.A(grf_1_rd1), .B(multiplexer_3_out), .ALUop(alucontrol_1_aluop_2), .Zero(alu_1_zero), .Result(out_8));
  ALUcontrol alucontrol_1 (.Func(out_2[5:0]), .ALUOp(controlunit_1_aluop_2_0), .ALUop_2(alucontrol_1_aluop_2));
  Multiplexer #(.width(32)) multiplexer_4 (
    .in0(adder_2_out), .in1(adder_3_out), .out(multiplexer_4_out), .sel(and_1_out));  // open: en
  and and_1 (and_1_out, controlunit_1_pcsrc, alu_1_zero);
  RAM #(.addrWidth(12), .dataWidth(32), .bus("separate")) ram_1 (
    .addr(out_8[13:2]), .din(out_9), .data(ram_1_data), .str(out_7), .clk(clk), .ld(controlunit_1_memread),
    .clr(reset));  // open: sel
  Multiplexer #(.width(32)) multiplexer_5 (
    .in0(ram_1_data), .in1(out_8), .out(multiplexer_5_out), .sel(controlunit_1_memtoreg));  // open: en

  // Other names for the same wires on the sheet: Instr[31:0] = out_2; Func[5:0] = out_2[5:0];
  //   Shamt[4:0] = out_2[10:6]; Rd[4:0] = out_2[15:11]; MemAddr[31:0] = out_8; MemData[31:0] = out_9;
  //   MemWrite = out_7; RegAddr[4:0] = out_5; RegData[31:0] = out_6; RegWrite = out_4

  // Notes on the sheet:
  //   contents of rom_1 (hex, n*v repeats v):
  //   34080004 3c09873d
endmodule

module ALU (
  input  [31:0] A,
  input  [31:0] B,
  input  [1:0] ALUop,
  output Zero,
  output [31:0] Result
);

  wire [31:0] addOut, andOut, orOut, subOut;

  Comparator #(.width(32)) comparator_1 (.a(A), .b(B), .eq(Zero));  // open: gt, lt
  assign andOut = A & B;  // AND_Gate and_1, 32 bits wide
  assign orOut = A | B;  // OR_Gate or_1, 32 bits wide
  Adder #(.width(32)) adder_1 (.a(A), .b(B), .out(addOut));  // open: cin, cout
  Subtractor #(.width(32)) subtractor_1 (.a(A), .b(B), .out(subOut));  // open: bin, bout
  Multiplexer #(.select(2), .width(32)) multiplexer_1 (
    .in0(andOut), .in1(orOut), .in2(addOut), .in3(subOut), .out(Result), .sel(ALUop));  // open: en

  // Other names for the same wires on the sheet: op[1:0] = ALUop
endmodule

module GRF (
  input  clk,
  input  reset,
  input  we,
  input  [4:0] Rr1,
  input  [4:0] Rr2,
  input  [4:0] Wr,
  input  [31:0] WD,
  output [31:0] RD1,
  output [31:0] RD2
);

  wire [31:0] _0a1, _0a2, _0a3, _0a4, _0a5, _0a6, _0a7, _0a8, _0a9, _0a10, _0a11, _0a12, _0a13, _0a14, _0a15,
       _0a16, _0a17, _0a18, _0a19, _0a20, _0a21, _0a22, _0a23, _0a24, _0a25, _0a26, _0a27, _0a28, _0a29,
       _0a30, _0a31, _0a32, _2a2, _2a3, _2a4, _2a5, _2a6, _2a7, _2a8, _2a9, _2a10, _2a11, _2a12, _2a13,
       _2a14, _2a15, _2a16, _2a17, _2a18, _2a19, _2a20, _2a21, _2a22, _2a23, _2a24, _2a25, _2a26, _2a27,
       _2a28, _2a29, _2a30, _2a31, _2a32;

  Demultiplexer #(.select(5), .width(32), .tristate("true")) demultiplexer_1 (
    .out1(_2a2), .out2(_2a3), .out3(_2a4), .out4(_2a5), .out5(_2a6), .out6(_2a7), .out7(_2a8), .out8(_2a9),
    .out9(_2a10), .out10(_2a11), .out11(_2a12), .out12(_2a13), .out13(_2a14), .out14(_2a15), .out15(_2a16),
    .out16(_2a17), .out17(_2a18), .out18(_2a19), .out19(_2a20), .out20(_2a21), .out21(_2a22), .out22(_2a23),
    .out23(_2a24), .out24(_2a25), .out25(_2a26), .out26(_2a27), .out27(_2a28), .out28(_2a29), .out29(_2a30),
    .out30(_2a31), .out31(_2a32), .in(WD), .sel(Wr));  // open: out0, en
  Register #(.width(32)) _0 (.D({32{1'b0}}), .en(we), .Q(_0a1), .clk(clk), .clr(reset));
  Register #(.width(32)) _4 (.D(_2a5), .en(we), .Q(_0a5), .clk(clk), .clr(reset));
  Register #(.width(32)) _8 (.D(_2a9), .en(we), .Q(_0a9), .clk(clk), .clr(reset));
  Register #(.width(32)) _12 (.D(_2a13), .en(we), .Q(_0a13), .clk(clk), .clr(reset));
  Register #(.width(32)) _16 (.D(_2a17), .en(we), .Q(_0a17), .clk(clk), .clr(reset));
  Register #(.width(32)) _20 (.D(_2a21), .en(we), .Q(_0a21), .clk(clk), .clr(reset));
  Register #(.width(32)) _24 (.D(_2a25), .en(we), .Q(_0a25), .clk(clk), .clr(reset));
  Register #(.width(32)) _28 (.D(_2a29), .en(we), .Q(_0a29), .clk(clk), .clr(reset));
  Register #(.width(32)) _1 (.D(_2a2), .en(we), .Q(_0a2), .clk(clk), .clr(reset));
  Register #(.width(32)) _5 (.D(_2a6), .en(we), .Q(_0a6), .clk(clk), .clr(reset));
  Register #(.width(32)) _9 (.D(_2a10), .en(we), .Q(_0a10), .clk(clk), .clr(reset));
  Register #(.width(32)) _13 (.D(_2a14), .en(we), .Q(_0a14), .clk(clk), .clr(reset));
  Register #(.width(32)) _17 (.D(_2a18), .en(we), .Q(_0a18), .clk(clk), .clr(reset));
  Register #(.width(32)) _21 (.D(_2a22), .en(we), .Q(_0a22), .clk(clk), .clr(reset));
  Register #(.width(32)) _25 (.D(_2a26), .en(we), .Q(_0a26), .clk(clk), .clr(reset));
  Register #(.width(32)) _29 (.D(_2a30), .en(we), .Q(_0a30), .clk(clk), .clr(reset));
  Register #(.width(32)) _2 (.D(_2a3), .en(we), .Q(_0a3), .clk(clk), .clr(reset));
  Register #(.width(32)) _6 (.D(_2a7), .en(we), .Q(_0a7), .clk(clk), .clr(reset));
  Register #(.width(32)) _10 (.D(_2a11), .en(we), .Q(_0a11), .clk(clk), .clr(reset));
  Register #(.width(32)) _14 (.D(_2a15), .en(we), .Q(_0a15), .clk(clk), .clr(reset));
  Register #(.width(32)) _18 (.D(_2a19), .en(we), .Q(_0a19), .clk(clk), .clr(reset));
  Register #(.width(32)) _22 (.D(_2a23), .en(we), .Q(_0a23), .clk(clk), .clr(reset));
  Register #(.width(32)) _26 (.D(_2a27), .en(we), .Q(_0a27), .clk(clk), .clr(reset));
  Register #(.width(32)) _30 (.D(_2a31), .en(we), .Q(_0a31), .clk(clk), .clr(reset));
  Register #(.width(32)) _3 (.D(_2a4), .en(we), .Q(_0a4), .clk(clk), .clr(reset));
  Register #(.width(32)) _7 (.D(_2a8), .en(we), .Q(_0a8), .clk(clk), .clr(reset));
  Register #(.width(32)) _11 (.D(_2a12), .en(we), .Q(_0a12), .clk(clk), .clr(reset));
  Register #(.width(32)) _15 (.D(_2a16), .en(we), .Q(_0a16), .clk(clk), .clr(reset));
  Register #(.width(32)) _19 (.D(_2a20), .en(we), .Q(_0a20), .clk(clk), .clr(reset));
  Register #(.width(32)) _23 (.D(_2a24), .en(we), .Q(_0a24), .clk(clk), .clr(reset));
  Register #(.width(32)) _27 (.D(_2a28), .en(we), .Q(_0a28), .clk(clk), .clr(reset));
  Register #(.width(32)) _31 (.D(_2a32), .en(we), .Q(_0a32), .clk(clk), .clr(reset));
  Multiplexer #(.select(5), .width(32)) multiplexer_1 (
    .in0(_0a1), .in1(_0a2), .in2(_0a3), .in3(_0a4), .in4(_0a5), .in5(_0a6), .in6(_0a7), .in7(_0a8),
    .in8(_0a9), .in9(_0a10), .in10(_0a11), .in11(_0a12), .in12(_0a13), .in13(_0a14), .in14(_0a15),
    .in15(_0a16), .in16(_0a17), .in17(_0a18), .in18(_0a19), .in19(_0a20), .in20(_0a21), .in21(_0a22),
    .in22(_0a23), .in23(_0a24), .in24(_0a25), .in25(_0a26), .in26(_0a27), .in27(_0a28), .in28(_0a29),
    .in29(_0a30), .in30(_0a31), .in31(_0a32), .out(RD1), .sel(Rr1));  // open: en
  Multiplexer #(.select(5), .width(32)) multiplexer_2 (
    .in0(_0a1), .in1(_0a2), .in2(_0a3), .in3(_0a4), .in4(_0a5), .in5(_0a6), .in6(_0a7), .in7(_0a8),
    .in8(_0a9), .in9(_0a10), .in10(_0a11), .in11(_0a12), .in12(_0a13), .in13(_0a14), .in14(_0a15),
    .in15(_0a16), .in16(_0a17), .in17(_0a18), .in18(_0a19), .in19(_0a20), .in20(_0a21), .in21(_0a22),
    .in22(_0a23), .in23(_0a24), .in24(_0a25), .in25(_0a26), .in26(_0a27), .in27(_0a28), .in28(_0a29),
    .in29(_0a30), .in30(_0a31), .in31(_0a32), .out(RD2), .sel(Rr2));  // open: en

  // Other names for the same wires on the sheet: _1a1[31:0] = _0a1; _1a2[31:0] = _0a2; _1a3[31:0] = _0a3;
  //   _1a4[31:0] = _0a4; _1a5[31:0] = _0a5; _1a6[31:0] = _0a6; _1a7[31:0] = _0a7; _1a8[31:0] = _0a8;
  //   _1a9[31:0] = _0a9; _1a10[31:0] = _0a10; _1a11[31:0] = _0a11; _1a12[31:0] = _0a12; _1a13[31:0] = _0a13;
  //   _1a14[31:0] = _0a14; _1a15[31:0] = _0a15; _1a16[31:0] = _0a16; _1a17[31:0] = _0a17; _1a18[31:0] = _0a18;
  //   _1a19[31:0] = _0a19; _1a20[31:0] = _0a20; _1a21[31:0] = _0a21; _1a22[31:0] = _0a22; _1a23[31:0] = _0a23;
  //   _1a24[31:0] = _0a24; _1a25[31:0] = _0a25; _1a26[31:0] = _0a26; _1a27[31:0] = _0a27; _1a28[31:0] = _0a28;
  //   _1a29[31:0] = _0a29; _1a30[31:0] = _0a30; _1a31[31:0] = _0a31; _1a32[31:0] = _0a32; A1[4:0] = Rr1;
  //   A2[4:0] = Rr2; A3[4:0] = Wr
endmodule

module EXT (
  input  [15:0] Input,
  output [31:0] Result
);


  assign Result = {Input, {16{1'b0}}};
endmodule

module ControlUnit (
  input  [5:0] Op,
  output PCSrc,
  output MemtoReg,
  output MemWrite,
  output MemRead,
  output [2:0] ALUOp_2_0,
  output SignOp,
  output RegDst,
  output ExtOp,
  output ALUSrc,
  output RegWrite
);

  wire andlist_1_beq, andlist_1_lui, andlist_1_lw, andlist_1_ori, \andlist_1_r类型 , andlist_1_sw;

  ANDlist andlist_1 (
    .Op5(Op[5]), .Op4(Op[4]), .Op3(Op[3]), .Op2(Op[2]), .Op1(Op[1]), .Op0(Op[0]), .\R类型 (\andlist_1_r类型 ),
    .ori(andlist_1_ori), .lw(andlist_1_lw), .sw(andlist_1_sw), .beq(andlist_1_beq), .lui(andlist_1_lui));
  ORIlist orilist_1 (
    .\R类型 (\andlist_1_r类型 ), .ori(andlist_1_ori), .lw(andlist_1_lw), .sw(andlist_1_sw), .beq(andlist_1_beq),
    .lui(andlist_1_lui), .RegDst(RegDst), .ALUSrc(ALUSrc), .MemtoReg(MemtoReg), .RegWrite(RegWrite),
    .MemWrite(MemWrite), .MemRead(MemRead), .PCSrc(PCSrc), .SignOp(SignOp), .ExtOp(ExtOp),
    .ALUOp_2_0(ALUOp_2_0));
endmodule

module ALUcontrol (
  input  [5:0] Func,
  input  [2:0] ALUOp,
  output [1:0] ALUop_2
);

  wire _00, _01, _10, _11, nFunc0, nFunc1, nFunc2, nFunc3, nFunc4, nFunc5;
  wire [1:0] _100out;

  not not_1 (nFunc5, Func[5]);
  not not_2 (nFunc4, Func[4]);
  and u__00 (_00, Func[5], nFunc4, nFunc3, Func[2], nFunc1, nFunc0);
  and u__01 (_01, Func[5], nFunc4, nFunc3, Func[2], nFunc1, Func[0]);
  and u__10 (_10, Func[5], nFunc4, nFunc3, nFunc2, nFunc1, nFunc0);
  and u__11 (_11, Func[5], nFunc4, nFunc3, nFunc2, Func[1], nFunc0);
  not not_3 (nFunc3, Func[3]);
  Multiplexer #(.select(3), .width(2)) multiplexer_1 (
    .in1(2'b01), .in2(2'b10), .in3(2'b11), .in4(_100out), .out(ALUop_2), .sel(ALUOp));  // open: in0, in5, in6, in7, en
  not not_4 (nFunc2, Func[2]);
  or or_1 (_100out[0], _01, _11);
  or or_2 (_100out[1], _10, _11);
  not not_5 (nFunc1, Func[1]);
  not not_6 (nFunc0, Func[0]);
endmodule

module ANDlist (
  input  Op5,
  input  Op4,
  input  Op3,
  input  Op2,
  input  Op1,
  input  Op0,
  output \R类型 ,
  output ori,
  output lw,
  output sw,
  output beq,
  output lui
);

  wire nOp0, nOp1, nOp2, nOp3, nOp4, nOp5;

  not not_1 (nOp5, Op5);
  not not_2 (nOp4, Op4);
  and \u_R类型  (\R类型 , nOp5, nOp4, nOp3, nOp2, nOp1, nOp0);
  and u_ori (ori, nOp5, nOp4, Op3, Op2, nOp1, Op0);
  and u_lw (lw, Op5, nOp4, nOp3, nOp2, Op1, Op0);
  and u_sw (sw, Op5, nOp4, Op3, nOp2, Op1, Op0);
  and u_beq (beq, nOp5, nOp4, nOp3, Op2, nOp1, nOp0);
  and u_lui (lui, nOp5, nOp4, Op3, Op2, Op1, Op0);
  not not_3 (nOp3, Op3);
  not not_4 (nOp2, Op2);
  not not_5 (nOp1, Op1);
  not not_6 (nOp0, Op0);
endmodule

module ORIlist (
  input  \R类型 ,
  input  ori,
  input  lw,
  input  sw,
  input  beq,
  input  lui,
  output RegDst,
  output ALUSrc,
  output MemtoReg,
  output RegWrite,
  output MemWrite,
  output MemRead,
  output PCSrc,
  output SignOp,
  output ExtOp,
  output [2:0] ALUOp_2_0
);

  or u_ALUSrc (ALUSrc, ori, lw, sw);
  or u_MemtoReg (MemtoReg, ori, \R类型 );
  or u_RegWrite (RegWrite, \R类型 , ori, lw, lui);
  or ALUOp1 (ALUOp_2_0[1], beq, lw, sw);
  or ALUOp0 (ALUOp_2_0[0], ori, beq);

  assign ALUOp_2_0[2] = \R类型 ;
  assign ExtOp = lui;
  assign MemRead = lw;
  assign MemWrite = sw;
  assign PCSrc = beq;
  assign RegDst = \R类型 ;
  assign SignOp = ori;
endmodule

module SIGNext (
  input  [15:0] Input,
  input  SignOp,
  output [31:0] Result
);

  wire [31:0] bit_extender_1_out, bit_extender_2_out;

  assign bit_extender_1_out = {{16{Input[15]}}, Input};  // Bit_Extender bit_extender_1
  assign bit_extender_2_out = {{16{1'b0}}, Input};  // Bit_Extender bit_extender_2
  Multiplexer #(.width(32)) multiplexer_1 (
    .in0(bit_extender_1_out), .in1(bit_extender_2_out), .out(Result), .sel(SignOp));  // open: en
endmodule
