// Logisim project Logisim_mod5.circ as structural Verilog: 1 circuit, main circuit mod5
module mod5 (
  input  In,
  output S0,
  output S1,
  output S2,
  output S3,
  output S4
);

  wire clock_1_out;
  wire [1:0] \状态 ;

  Register #(.width(2)) register_1 (.D({\状态 [0], In}), .Q(\状态 ), .clk(clock_1_out));  // open: en, clr
  Clock clock_1 (.out(clock_1_out));
  Decoder #(.select(2)) decoder_1 (.out0(S1), .out1(S2), .out2(S4), .out3(S3), .sel({\状态 [0], In}));  // open: en

  assign S0 = 1'b0;
endmodule
