// Logisim project P0_L0_CRC.circ as structural Verilog: 2 circuits, main circuit CRC
module CRC (
  input  [7:0] A,
  input  [3:0] B,
  output [10:0] C
);

  wire [2:0] _1_c, _2_c, _3_c, _4_c, _5_c, _6_c, _7_c;

  crc4 _1 (.A(A[7:4]), .B(B), .C(_1_c));  // open: D
  crc4 _2 (.A({_1_c, A[3]}), .B(B), .C(_2_c));  // open: D
  crc4 _3 (.A({_2_c, A[2]}), .B(B), .C(_3_c));  // open: D
  crc4 _4 (.A({_3_c, A[1]}), .B(B), .C(_4_c));  // open: D
  crc4 _5 (.A({_4_c, A[0]}), .B(B), .C(_5_c));  // open: D
  crc4 _6 (.A({_5_c, 1'b0}), .B(B), .C(_6_c));  // open: D
  crc4 _7 (.A({_6_c, 1'b0}), .B(B), .C(_7_c));  // open: D
  crc4 _8 (.A({_7_c, 1'b0}), .B(B), .C(C[2:0]));  // open: D

  assign C[10:3] = A;
endmodule

// D
module crc4 (
  input  [3:0] A,
  input  [3:0] B,
  output [2:0] C,
  output D
);

  wire [3:0] xor_1_out;

  assign xor_1_out = A ^ B;  // XOR_Gate xor_1, 4 bits wide
  Comparator #(.width(1)) comparator_1 (.a(A[3]), .b(1'b1), .eq(D));  // open: gt, lt
  Multiplexer #(.width(3)) multiplexer_1 (.in0(A[2:0]), .in1(xor_1_out[2:0]), .out(C), .sel(D));  // open: en
endmodule
