// Logisim project P0_L0_FSM.circ as structural Verilog: 3 circuits, main circuit fsm
module fsm (
  input  CLR,
  input  [1:0] In,
  output Z
);

  wire clock_1_out;
  wire [2:0] change_1_nsit, multiplexer_1_out, register_1_q;

  change change_1 (.in(In), .sit(register_1_q), .nsit(change_1_nsit));
  Multiplexer #(.width(3)) multiplexer_1 (
    .in0(change_1_nsit), .in1(3'b000), .out(multiplexer_1_out), .sel(CLR));  // open: en
  Register #(.width(3)) register_1 (.D(multiplexer_1_out), .Q(register_1_q), .clk(clock_1_out));  // open: en, clr
  Clock clock_1 (.out(clock_1_out));
  out out_1 (.in(In), .sit(register_1_q), .z(Z));
endmodule

module change (
  input  [1:0] in,
  input  [2:0] sit,
  output [2:0] nsit
);

  wire and_2_out, and_3_out, and_4_out, and_5_out, and_6_out, and_7_out, and_8_out, and_9_out, not_1_out,
       not_2_out, not_3_out, not_4_out, not_5_out, not_6_out, not_7_out, not_8_out, not_9_out, not_10_out,
       not_11_out, not_12_out, not_13_out, not_14_out, not_15_out, not_16_out, not_17_out;

  not not_1 (not_1_out, in[0]);
  not not_2 (not_2_out, sit[1]);
  not not_3 (not_3_out, in[1]);
  not not_4 (not_4_out, sit[1]);
  not not_5 (not_5_out, in[0]);
  not not_6 (not_6_out, sit[0]);
  not not_7 (not_7_out, in[1]);
  not not_8 (not_8_out, sit[0]);
  not not_9 (not_9_out, in[0]);
  not not_10 (not_10_out, sit[1]);
  not not_11 (not_11_out, sit[0]);
  not not_12 (not_12_out, in[1]);
  not not_13 (not_13_out, sit[1]);
  not not_14 (not_14_out, in[0]);
  not not_15 (not_15_out, sit[0]);
  not not_16 (not_16_out, in[0]);
  not not_17 (not_17_out, in[1]);
  and and_1 (nsit[2], sit[1], sit[0], not_1_out);
  and and_2 (and_2_out, not_2_out, sit[0], not_3_out);
  and and_3 (and_3_out, not_4_out, sit[0], not_5_out);
  and and_4 (and_4_out, sit[1], not_6_out, not_7_out);
  and and_5 (and_5_out, sit[1], not_8_out, not_9_out);
  and and_6 (and_6_out, not_10_out, not_11_out, not_12_out, in[0]);
  and and_7 (and_7_out, not_13_out, sit[0], not_14_out);
  and and_8 (and_8_out, sit[1], not_15_out, not_16_out);
  and and_9 (and_9_out, sit[1], sit[0], not_17_out, in[0]);
  or or_1 (nsit[1], and_2_out, and_3_out, and_4_out, and_5_out);
  or or_2 (nsit[0], and_6_out, and_7_out, and_8_out, and_9_out);

  // Other names for the same wires on the sheet: s0 = in[0]; s1 = in[1]; _0 = nsit[0]; _1 = nsit[1]; _2 = nsit[2];
  //   in0 = sit[1]
endmodule

module out (
  input  [1:0] in,
  input  [2:0] sit,
  output z
);

  wire not_1_out, not_2_out;

  not not_1 (not_1_out, sit[2]);
  not not_2 (not_2_out, in[0]);
  and and_1 (z, not_1_out, sit[1], sit[0], not_2_out);

  // Other names for the same wires on the sheet: a0 = in[0]; s0 = sit[0]; _2 = sit[1]; _1 = sit[2]
endmodule
