// Logisim project P0_L0_GRF.circ as structural Verilog: 1 circuit, main circuit grf
module grf (
  input  clk,
  input  reset,
  input  WE,
  input  [4:0] A1,
  input  [4:0] A2,
  input  [4:0] A3,
  input  [31:0] WD,
  output [31:0] RD1,
  output [31:0] RD2
);

  wire [31:0] _0a1, _0a2, _0a3, _0a4, _0a5, _0a6, _0a7, _0a8, _0a9, _0a10, _0a11, _0a12, _0a13, _0a14, _0a15,
       _0a16, _0a17, _0a18, _0a19, _0a20, _0a21, _0a22, _0a23, _0a24, _0a25, _0a26, _0a27, _0a28, _0a29,
       _0a30, _0a31, _0a32, _2a2, _2a3, _2a4, _2a5, _2a6, _2a7, _2a8, _2a9, _2a10, _2a11, _2a12, _2a13,
       _2a14, _2a15, _2a16, _2a17, _2a18, _2a19, _2a20, _2a21, _2a22, _2a23, _2a24, _2a25, _2a26, _2a27,
       _2a28, _2a29, _2a30, _2a31, _2a32;

  Demultiplexer #(.select(5), .width(32), .tristate("true")) demultiplexer_1 (
    .out1(_2a2), .out2(_2a3), .out3(_2a4), .out4(_2a5), .out5(_2a6), .out6(_2a7), .out7(_2a8), .out8(_2a9),
    .out9(_2a10), .out10(_2a11), .out11(_2a12), .out12(_2a13), .out13(_2a14), .out14(_2a15), .out15(_2a16),
    .out16(_2a17), .out17(_2a18), .out18(_2a19), .out19(_2a20), .out20(_2a21), .out21(_2a22), .out22(_2a23),
    .out23(_2a24), .out24(_2a25), .out25(_2a26), .out26(_2a27), .out27(_2a28), .out28(_2a29), .out29(_2a30),
    .out30(_2a31), .out31(_2a32), .in(WD), .sel(A3));  // open: out0, en
  Register #(.width(32)) _0 (.D({32{1'b0}}), .en(WE), .Q(_0a1), .clk(clk), .clr(reset));
  Register #(.width(32)) _4 (.D(_2a5), .en(WE), .Q(_0a5), .clk(clk), .clr(reset));
  Register #(.width(32)) _8 (.D(_2a9), .en(WE), .Q(_0a9), .clk(clk), .clr(reset));
  Register #(.width(32)) _12 (.D(_2a13), .en(WE), .Q(_0a13), .clk(clk), .clr(reset));
  Register #(.width(32)) _16 (.D(_2a17), .en(WE), .Q(_0a17), .clk(clk), .clr(reset));
  Register #(.width(32)) _20 (.D(_2a21), .en(WE), .Q(_0a21), .clk(clk), .clr(reset));
  Register #(.width(32)) _24 (.D(_2a25), .en(WE), .Q(_0a25), .clk(clk), .clr(reset));
  Register #(.width(32)) _28 (.D(_2a29), .en(WE), .Q(_0a29), .clk(clk), .clr(reset));
  Register #(.width(32)) _1 (.D(_2a2), .en(WE), .Q(_0a2), .clk(clk), .clr(reset));
  Register #(.width(32)) _5 (.D(_2a6), .en(WE), .Q(_0a6), .clk(clk), .clr(reset));
  Register #(.width(32)) _9 (.D(_2a10), .en(WE), .Q(_0a10), .clk(clk), .clr(reset));
  Register #(.width(32)) _13 (.D(_2a14), .en(WE), .Q(_0a14), .clk(clk), .clr(reset));
  Register #(.width(32)) _17 (.D(_2a18), .en(WE), .Q(_0a18), .clk(clk), .clr(reset));
  Register #(.width(32)) _21 (.D(_2a22), .en(WE), .Q(_0a22), .clk(clk), .clr(reset));
  Register #(.width(32)) _25 (.D(_2a26), .en(WE), .Q(_0a26), .clk(clk), .clr(reset));
  Register #(.width(32)) _29 (.D(_2a30), .en(WE), .Q(_0a30), .clk(clk), .clr(reset));
  Register #(.width(32)) _2 (.D(_2a3), .en(WE), .Q(_0a3), .clk(clk), .clr(reset));
  Register #(.width(32)) _6 (.D(_2a7), .en(WE), .Q(_0a7), .clk(clk), .clr(reset));
  Register #(.width(32)) _10 (.D(_2a11), .en(WE), .Q(_0a11), .clk(clk), .clr(reset));
  Register #(.width(32)) _14 (.D(_2a15), .en(WE), .Q(_0a15), .clk(clk), .clr(reset));
  Register #(.width(32)) _18 (.D(_2a19), .en(WE), .Q(_0a19), .clk(clk), .clr(reset));
  Register #(.width(32)) _22 (.D(_2a23), .en(WE), .Q(_0a23), .clk(clk), .clr(reset));
  Register #(.width(32)) _26 (.D(_2a27), .en(WE), .Q(_0a27), .clk(clk), .clr(reset));
  Register #(.width(32)) _30 (.D(_2a31), .en(WE), .Q(_0a31), .clk(clk), .clr(reset));
  Register #(.width(32)) _3 (.D(_2a4), .en(WE), .Q(_0a4), .clk(clk), .clr(reset));
  Register #(.width(32)) _7 (.D(_2a8), .en(WE), .Q(_0a8), .clk(clk), .clr(reset));
  Register #(.width(32)) _11 (.D(_2a12), .en(WE), .Q(_0a12), .clk(clk), .clr(reset));
  Register #(.width(32)) _15 (.D(_2a16), .en(WE), .Q(_0a16), .clk(clk), .clr(reset));
  Register #(.width(32)) _19 (.D(_2a20), .en(WE), .Q(_0a20), .clk(clk), .clr(reset));
  Register #(.width(32)) _23 (.D(_2a24), .en(WE), .Q(_0a24), .clk(clk), .clr(reset));
  Register #(.width(32)) _27 (.D(_2a28), .en(WE), .Q(_0a28), .clk(clk), .clr(reset));
  Register #(.width(32)) _31 (.D(_2a32), .en(WE), .Q(_0a32), .clk(clk), .clr(reset));
  Multiplexer #(.select(5), .width(32)) multiplexer_1 (
    .in0(_0a1), .in1(_0a2), .in2(_0a3), .in3(_0a4), .in4(_0a5), .in5(_0a6), .in6(_0a7), .in7(_0a8),
    .in8(_0a9), .in9(_0a10), .in10(_0a11), .in11(_0a12), .in12(_0a13), .in13(_0a14), .in14(_0a15),
    .in15(_0a16), .in16(_0a17), .in17(_0a18), .in18(_0a19), .in19(_0a20), .in20(_0a21), .in21(_0a22),
    .in22(_0a23), .in23(_0a24), .in24(_0a25), .in25(_0a26), .in26(_0a27), .in27(_0a28), .in28(_0a29),
    .in29(_0a30), .in30(_0a31), .in31(_0a32), .out(RD1), .sel(A1));  // open: en
  Multiplexer #(.select(5), .width(32)) multiplexer_2 (
    .in0(_0a1), .in1(_0a2), .in2(_0a3), .in3(_0a4), .in4(_0a5), .in5(_0a6), .in6(_0a7), .in7(_0a8),
    .in8(_0a9), .in9(_0a10), .in10(_0a11), .in11(_0a12), .in12(_0a13), .in13(_0a14), .in14(_0a15),
    .in15(_0a16), .in16(_0a17), .in17(_0a18), .in18(_0a19), .in19(_0a20), .in20(_0a21), .in21(_0a22),
    .in22(_0a23), .in23(_0a24), .in24(_0a25), .in25(_0a26), .in26(_0a27), .in27(_0a28), .in28(_0a29),
    .in29(_0a30), .in30(_0a31), .in31(_0a32), .out(RD2), .sel(A2));  // open: en

  // Other names for the same wires on the sheet: _1a1[31:0] = _0a1; _1a2[31:0] = _0a2; _1a3[31:0] = _0a3;
  //   _1a4[31:0] = _0a4; _1a5[31:0] = _0a5; _1a6[31:0] = _0a6; _1a7[31:0] = _0a7; _1a8[31:0] = _0a8;
  //   _1a9[31:0] = _0a9; _1a10[31:0] = _0a10; _1a11[31:0] = _0a11; _1a12[31:0] = _0a12; _1a13[31:0] = _0a13;
  //   _1a14[31:0] = _0a14; _1a15[31:0] = _0a15; _1a16[31:0] = _0a16; _1a17[31:0] = _0a17; _1a18[31:0] = _0a18;
  //   _1a19[31:0] = _0a19; _1a20[31:0] = _0a20; _1a21[31:0] = _0a21; _1a22[31:0] = _0a22; _1a23[31:0] = _0a23;
  //   _1a24[31:0] = _0a24; _1a25[31:0] = _0a25; _1a26[31:0] = _0a26; _1a27[31:0] = _0a27; _1a28[31:0] = _0a28;
  //   _1a29[31:0] = _0a29; _1a30[31:0] = _0a30; _1a31[31:0] = _0a31; _1a32[31:0] = _0a32
endmodule
