// Logisim project P0_L1_ftoi.circ as structural Verilog: 1 circuit, main circuit ftoi
module ftoi (
  input  [15:0] in_1,
  output [31:0] out_2
);

  wire comparator_1_eq, comparator_2_eq, comparator_3_eq, comparator_4_lt;
  wire [7:0] subtractor_1_out, subtractor_2_out;
  wire [31:0] _1, adder_1_out, not_1_out, shifter_1_out, shifter_2_out, x, xx;

  assign not_1_out = ~x;  // NOT_Gate not_1, 32 bits wide
  Adder #(.width(32)) adder_1 (.a(not_1_out), .b(32'h1), .out(adder_1_out));  // open: cin, cout
  Comparator #(.width(1)) comparator_1 (.a(in_1[15]), .b(1'b0), .eq(comparator_1_eq));  // open: gt, lt
  Comparator #(.width(5)) comparator_2 (.a(in_1[14:10]), .b({5{1'b0}}), .eq(comparator_2_eq));  // open: gt, lt
  Multiplexer #(.width(32)) multiplexer_1 (.in0(adder_1_out), .in1(x), .out(xx), .sel(comparator_1_eq));  // open: en
  Multiplexer #(.width(32)) multiplexer_2 (.in0(xx), .in1({32{1'b0}}), .out(_1), .sel(comparator_2_eq));  // open: en
  Comparator #(.width(5)) comparator_3 (.a(in_1[14:10]), .b({5{1'b1}}), .eq(comparator_3_eq));  // open: gt, lt
  Subtractor subtractor_1 (.a({3'b000, in_1[14:10]}), .b(8'h19), .out(subtractor_1_out));  // open: bin, bout
  Subtractor subtractor_2 (.a(8'h19), .b({3'b000, in_1[14:10]}), .out(subtractor_2_out));  // open: bin, bout
  Multiplexer #(.width(32)) multiplexer_3 (.in0(_1), .in1({32{1'b0}}), .out(out_2), .sel(comparator_3_eq));  // open: en
  Shifter #(.width(32)) shifter_1 (.in({22'h1, in_1[9:0]}), .\dist (subtractor_1_out[4:0]), .out(shifter_1_out));
  Shifter #(.width(32), .shift("lr")) shifter_2 (
    .in({22'h1, in_1[9:0]}), .\dist (subtractor_2_out[4:0]), .out(shifter_2_out));
  Comparator comparator_4 (.a({3'b000, in_1[14:10]}), .b(8'h19), .lt(comparator_4_lt));  // open: gt, eq
  Multiplexer #(.width(32)) multiplexer_4 (
    .in0(shifter_1_out), .in1(shifter_2_out), .out(x), .sel(comparator_4_lt));  // open: en

  // Other names for the same wires on the sheet: _2[9:0] = in_1[9:0]; _3[4:0] = in_1[14:10]; x3[4:0] = in_1[14:10]
endmodule
