// Logisim project P0_L1_navigation_2020.circ as structural Verilog: 3 circuits, main circuit navigation
module navigation (
  input  [1:0] dir,
  input  clk,
  input  reset,
  output arrive,
  output hit
);

  wire [3:0] change_1_ss, register_1_q;

  change change_1 (.dir(dir), .s(register_1_q), .ss(change_1_ss));
  Register #(.width(4)) register_1 (.D(change_1_ss), .Q(register_1_q), .clk(clk), .clr(reset));  // open: en
  out out_1 (.s(register_1_q), .arrive(arrive), .hit(hit));
endmodule

module change (
  input  [1:0] dir,
  input  [3:0] s,
  output [3:0] ss
);

  wire and_1_out, and_2_out, and_3_out, and_4_out, and_5_out, and_6_out, and_7_out, and_8_out, and_9_out,
       and_10_out, and_11_out, and_12_out, and_13_out, and_14_out, and_15_out, and_16_out, and_17_out,
       and_18_out, and_19_out, and_20_out, and_21_out, and_22_out, and_23_out, and_24_out, and_25_out,
       and_26_out, and_27_out, and_28_out, and_29_out, and_30_out, not_1_out, not_2_out, not_3_out,
       not_4_out, not_5_out, not_6_out, not_7_out, not_8_out, not_9_out, not_10_out, not_11_out, not_12_out,
       not_13_out, not_14_out, not_15_out, not_16_out, not_17_out, not_18_out, not_19_out, not_20_out,
       not_21_out, not_22_out, not_23_out, not_24_out, not_25_out, not_26_out, not_27_out, not_28_out,
       not_29_out, not_30_out, not_31_out, not_32_out, not_33_out, not_34_out, not_35_out, not_36_out,
       not_37_out, not_38_out, not_39_out, not_40_out, not_41_out, not_42_out, not_43_out, not_44_out,
       not_45_out, not_46_out, not_47_out, not_48_out, not_49_out, not_50_out, not_51_out, not_52_out,
       not_53_out, not_54_out, not_55_out, not_56_out, not_57_out;

  not not_1 (not_1_out, s[2]);
  not not_2 (not_2_out, dir[1]);
  not not_3 (not_3_out, dir[0]);
  not not_4 (not_4_out, s[2]);
  not not_5 (not_5_out, dir[1]);
  not not_6 (not_6_out, dir[0]);
  not not_7 (not_7_out, s[2]);
  not not_8 (not_8_out, s[0]);
  not not_9 (not_9_out, dir[1]);
  not not_10 (not_10_out, s[3]);
  not not_11 (not_11_out, s[2]);
  not not_12 (not_12_out, s[1]);
  not not_13 (not_13_out, s[0]);
  not not_14 (not_14_out, s[1]);
  not not_15 (not_15_out, s[2]);
  not not_16 (not_16_out, s[0]);
  not not_17 (not_17_out, dir[0]);
  not not_18 (not_18_out, s[2]);
  not not_19 (not_19_out, dir[1]);
  not not_20 (not_20_out, s[1]);
  not not_21 (not_21_out, s[1]);
  not not_22 (not_22_out, s[0]);
  not not_23 (not_23_out, dir[1]);
  not not_24 (not_24_out, dir[0]);
  not not_25 (not_25_out, s[2]);
  not not_26 (not_26_out, s[1]);
  not not_27 (not_27_out, dir[1]);
  not not_28 (not_28_out, s[2]);
  not not_29 (not_29_out, s[1]);
  not not_30 (not_30_out, s[0]);
  not not_31 (not_31_out, dir[1]);
  not not_32 (not_32_out, s[2]);
  not not_33 (not_33_out, s[0]);
  not not_34 (not_34_out, dir[0]);
  not not_35 (not_35_out, s[0]);
  not not_36 (not_36_out, dir[1]);
  not not_37 (not_37_out, s[0]);
  not not_38 (not_38_out, dir[1]);
  not not_39 (not_39_out, dir[0]);
  not not_40 (not_40_out, s[3]);
  not not_41 (not_41_out, s[2]);
  not not_42 (not_42_out, s[1]);
  not not_43 (not_43_out, s[0]);
  not not_44 (not_44_out, s[3]);
  not not_45 (not_45_out, s[2]);
  not not_46 (not_46_out, s[0]);
  not not_47 (not_47_out, s[2]);
  not not_48 (not_48_out, s[0]);
  not not_49 (not_49_out, dir[0]);
  not not_50 (not_50_out, s[1]);
  not not_51 (not_51_out, dir[1]);
  not not_52 (not_52_out, dir[0]);
  not not_53 (not_53_out, dir[0]);
  not not_54 (not_54_out, s[1]);
  not not_55 (not_55_out, s[0]);
  not not_56 (not_56_out, dir[1]);
  not not_57 (not_57_out, dir[0]);
  and and_1 (and_1_out, not_1_out, s[1], s[0], not_2_out, not_3_out);
  and and_2 (and_2_out, not_4_out, s[1], s[0], dir[1], dir[0]);
  and and_3 (and_3_out, s[3], not_5_out, not_6_out);
  and and_4 (and_4_out, s[3], dir[1], dir[0]);
  and and_5 (and_5_out, not_7_out, not_8_out, not_9_out, dir[0]);
  and and_6 (and_6_out, not_10_out, not_11_out, not_12_out, not_13_out, dir[1]);
  and and_7 (and_7_out, not_14_out, s[0], dir[1], dir[0]);
  and and_8 (and_8_out, not_15_out, s[1], not_16_out, not_17_out);
  and and_9 (and_9_out, not_18_out, s[1], not_19_out, dir[0]);
  and and_10 (and_10_out, s[2], not_20_out, s[0], dir[0]);
  and and_11 (and_11_out, s[2], not_21_out, s[0], dir[1]);
  and and_12 (and_12_out, s[2], s[1], not_22_out, dir[1], dir[0]);
  and and_13 (and_13_out, s[2], s[1], s[0], not_23_out);
  and and_14 (and_14_out, s[2], s[1], s[0], not_24_out);
  and and_15 (and_15_out, not_25_out, not_26_out, s[0], not_27_out);
  and and_16 (and_16_out, not_28_out, not_29_out, s[0], dir[0]);
  and and_17 (and_17_out, s[1], not_30_out, not_31_out, dir[0]);
  and and_18 (and_18_out, not_32_out, s[1], not_33_out, dir[1], not_34_out);
  and and_19 (and_19_out, s[2], s[1], not_35_out, not_36_out);
  and and_20 (and_20_out, s[2], s[1], not_37_out, dir[0]);
  and and_21 (and_21_out, s[2], s[1], not_38_out, dir[0]);
  and and_22 (and_22_out, s[2], s[1], s[0], dir[1], not_39_out);
  and and_23 (and_23_out, not_40_out, not_41_out, not_42_out, not_43_out);
  and and_24 (and_24_out, not_44_out, not_45_out, not_46_out, dir[0]);
  and and_25 (and_25_out, not_47_out, not_48_out, dir[1], not_49_out);
  and and_26 (and_26_out, not_50_out, s[0], not_51_out, not_52_out);
  and and_27 (and_27_out, s[1], s[0], dir[1], not_53_out);
  and and_28 (and_28_out, s[2], not_54_out, s[0]);
  and and_29 (and_29_out, s[2], s[0], dir[0]);
  and and_30 (and_30_out, s[2], s[1], not_55_out, not_56_out, not_57_out);
  or or_1 (ss[3], and_1_out, and_2_out, and_3_out, and_4_out);
  or or_2 (ss[2], and_5_out, and_6_out, and_7_out, and_8_out, and_9_out, and_10_out, and_11_out, and_12_out, and_13_out, and_14_out);
  or or_3 (ss[1], and_15_out, and_16_out, and_17_out, and_18_out, and_19_out, and_20_out, and_21_out, and_22_out);
  or or_4 (ss[0], and_23_out, and_24_out, and_25_out, and_26_out, and_27_out, and_28_out, and_29_out, and_30_out);

  // Other names for the same wires on the sheet: d0 = dir[0]; d1 = dir[1]
endmodule

module out (
  input  [3:0] s,
  output arrive,
  output hit
);

  wire and_1_out, and_2_out, not_1_out, not_2_out, not_3_out;

  not not_1 (not_1_out, s[3]);
  not not_2 (not_2_out, s[1]);
  not not_3 (not_3_out, s[0]);
  and and_1 (and_1_out, s[2], s[0]);
  and and_2 (and_2_out, s[2], s[1]);
  and and_3 (arrive, not_1_out, s[2], not_2_out, not_3_out);
  or or_1 (hit, and_1_out, and_2_out, s[3]);
endmodule
