// Logisim project P0_L2_nonexist_2023.circ as structural Verilog: 2 circuits, main circuit main
module main (
  input  [7:0] in_1,
  input  [7:0] in_2,
  input  [7:0] in_3,
  input  [7:0] in_4,
  input  [7:0] in_5,
  output [7:0] out_6
);

  wire _1, _2, _3, _4, _5, _6, _7, _8, _11, _12, _13, _14, _15, _16, _17, _18, _21, _22, _23, _24, _25, _26,
       _27, _28, _31, _32, _33, _34, _35, _36, _37, _38, _41, _42, _43, _44, _45, _46, _47, _48, _51, _52,
       _53, _54, _55, _56, _57, _58;
  wire [2:0] choose_1_out_2, choose_2_out_2, choose_3_out_2, choose_4_out_2, choose_5_out_2;

  Decoder #(.select(3)) decoder_1 (
    .out0(_11), .out1(_12), .out2(_13), .out3(_14), .out4(_15), .out5(_16), .out6(_17), .out7(_18),
    .sel(choose_1_out_2));  // open: en
  choose choose_1 (.in_1(in_1), .out_2(choose_1_out_2));
  Decoder #(.select(3)) decoder_2 (
    .out0(_21), .out1(_22), .out2(_23), .out3(_24), .out4(_25), .out5(_26), .out6(_27), .out7(_28),
    .sel(choose_2_out_2));  // open: en
  choose choose_2 (.in_1(in_2), .out_2(choose_2_out_2));
  Decoder #(.select(3)) decoder_3 (
    .out0(_31), .out1(_32), .out2(_33), .out3(_34), .out4(_35), .out5(_36), .out6(_37), .out7(_38),
    .sel(choose_3_out_2));  // open: en
  choose choose_3 (.in_1(in_3), .out_2(choose_3_out_2));
  Decoder #(.select(3)) decoder_4 (
    .out0(_41), .out1(_42), .out2(_43), .out3(_44), .out4(_45), .out5(_46), .out6(_47), .out7(_48),
    .sel(choose_4_out_2));  // open: en
  choose choose_4 (.in_1(in_4), .out_2(choose_4_out_2));
  Decoder #(.select(3)) decoder_5 (
    .out0(_51), .out1(_52), .out2(_53), .out3(_54), .out4(_55), .out5(_56), .out6(_57), .out7(_58),
    .sel(choose_5_out_2));  // open: en
  choose choose_5 (.in_1(in_5), .out_2(choose_5_out_2));
  or or_1 (_1, _11, _21, _31, _41, _51);
  or or_2 (_2, _12, _22, _32, _42, _52);
  or or_3 (_3, _13, _23, _33, _43, _53);
  or or_4 (_4, _14, _24, _34, _44, _54);
  or or_5 (_5, _15, _25, _35, _45, _55);
  or or_6 (_6, _16, _26, _36, _46, _56);
  or or_7 (_7, _17, _27, _37, _47, _57);
  or or_8 (_8, _18, _28, _38, _48, _58);
  BitFinder #(.\type ("low0")) bitfinder_1 (
    .in({_8, _7, _6, _5, _4, _3, _2, 1'b1}), .index(out_6[2:0]));  // open: found

  assign out_6[7:3] = {5{1'b0}};

  // Other names for the same wires on the sheet: sle[7:1] = {_8, _7, _6, _5, _4, _3, _2}
endmodule

module choose (
  input  [7:0] in_1,
  output [2:0] out_2
);

  wire comparator_1_gt;
  wire [7:3] multiplexer_1_out;

  Multiplexer #(.width(8)) multiplexer_1 (
    .in0(in_1), .in1(8'h6), .out({multiplexer_1_out, out_2}), .sel(comparator_1_gt));  // open: en
  Comparator comparator_1 (.a(in_1), .b(8'h6), .gt(comparator_1_gt));  // open: eq, lt
endmodule
